# Fritzing sketch schematics (saved by Fritzing 0.9.3b)
breadboards: 1

parts:
  Part1 = Arduino Uno (Rev3)
  LED1 = LED - 5mm [color="Red (633nm)" package="5 mm [THT]"]
  R1 = Resistor [tolerance=±5% resistance=220 package=THT]
  LED2 = LED - 5mm [color="Yellow (592nm)" package="5 mm [THT]"]
  R2 = Resistor [tolerance=±5% resistance=220 package=THT]

nets:
  N1: Part1.D5_PWM, R1.Pin_0
  N2: Part1.D6_PWM, R2.Pin_0
  N3: Part1.GND, LED2.anode
  N4: LED1.cathode, R1.Pin_1
  N5: LED2.cathode, R2.Pin_1
